# Fritzing sketch schaltplan-taster (saved by Fritzing 0.9.3b)
breadboards: 1

parts:
  Bauteil1 = Arduino Uno (Rev3)
  S1 = Pushbutton [package="[THT]"]
  R1 = Resistor [tolerance=±5% resistance=1k package=THT]

nets:
  N1: Bauteil1.GND, R1.Pin_0
  N2: Bauteil1.D3_PWM, S1.Pin_3, S1.Pin_4, R1.Pin_1
  N3: Bauteil1.5V, S1.Pin_1, S1.Pin_2
