# Fritzing sketch schaltplan_blink (saved by Fritzing 0.9.2b)
breadboards: 1

parts:
  Bauteil1 = Arduino Uno (Rev3)
  R1 = Resistor [tolerance=±5% resistance=330 package=THT]
  LED1 = LED - 5mm [color="Red (633nm)" package="5 mm [THT]"]

nets:
  N1: Bauteil1.D13/SCK, LED1.anode
  N2: Bauteil1.GND, R1.Pin_0
  N3: R1.Pin_1, LED1.cathode
