# Fritzing sketch schaltplan_dimm (saved by Fritzing 0.9.2b)
breadboards: 1

parts:
  Bauteil1 = Arduino Uno (Rev3)
  LED1 = LED - 5mm [color="Red (633nm)" package="5 mm [THT]"]
  R5 = Resistor [tolerance=±5% resistance=330 package=THT]

nets:
  N1: Bauteil1.D10_PWM/SS, R5.Pin_1
  N2: Bauteil1.GND, LED1.cathode
  N3: LED1.anode, R5.Pin_0
