# Fritzing sketch schaltplan_lauf (saved by Fritzing 0.9.2b)
breadboards: 1

parts:
  Bauteil1 = Arduino Uno (Rev3)
  LED1 = LED - 5mm [color="Red (633nm)" package="5 mm [THT]"]
  LED2 = LED - 5mm [color="Red (633nm)" package="5 mm [THT]"]
  LED3 = LED - 5mm [color="Red (633nm)" package="5 mm [THT]"]
  LED4 = LED - 5mm [color="Red (633nm)" package="5 mm [THT]"]
  LED5 = LED - 5mm [color="Red (633nm)" package="5 mm [THT]"]
  R1 = Resistor [tolerance=±5% resistance=330 package=THT]
  R2 = Resistor [tolerance=±5% resistance=330 package=THT]
  R3 = Resistor [tolerance=±5% resistance=330 package=THT]
  R4 = Resistor [tolerance=±5% resistance=330 package=THT]
  R5 = Resistor [tolerance=±5% resistance=330 package=THT]

nets:
  N1: Bauteil1.GND, LED1.cathode, LED2.cathode, LED3.cathode, LED4.cathode, LED5.cathode
  N2: Bauteil1.D2, R3.Pin_1
  N3: Bauteil1.D3_PWM, R1.Pin_1
  N4: Bauteil1.D4, R2.Pin_1
  N5: Bauteil1.D5_PWM, R4.Pin_1
  N6: Bauteil1.D6_PWM, R5.Pin_1
  N7: LED1.anode, R5.Pin_0
  N8: LED2.anode, R4.Pin_0
  N9: LED3.anode, R2.Pin_0
  N10: LED4.anode, R1.Pin_0
  N11: LED5.anode, R3.Pin_0
